// Digital circuit 8bit-register.dig as structural Verilog
module _8bit_register (
  input  in_2,
  input  in_3,
  input  clk,
  output out_1
);

  wire d_ff_1_nq, d_ff_2_nq, d_ff_3_nq, d_ff_4_nq, d_ff_5_nq, d_ff_6_nq, d_ff_7_nq, d_ff_8_nq;

  xor xor_1 (out_1, in_2, in_3);
  Switch switch_1 (.B(out_1));  // open: A
  D_FF d_ff_1 (.D(out_1), .C(clk), .nQ(d_ff_1_nq));  // open: Q
  LED led_1 (.in(d_ff_1_nq));
  D_FF d_ff_2 (.D(out_1), .C(clk), .nQ(d_ff_2_nq));  // open: Q
  LED led_2 (.in(d_ff_2_nq));
  Switch switch_2 (.A(clk), .B(clk));
  D_FF d_ff_3 (.D(out_1), .C(clk), .nQ(d_ff_3_nq));  // open: Q
  LED led_3 (.in(d_ff_3_nq));
  D_FF d_ff_4 (.D(out_1), .C(clk), .nQ(d_ff_4_nq));  // open: Q
  D_FF d_ff_5 (.D(out_1), .C(clk), .nQ(d_ff_5_nq));  // open: Q
  LED led_4 (.in(d_ff_4_nq));
  LED led_5 (.in(d_ff_5_nq));
  D_FF d_ff_6 (.D(out_1), .C(clk), .nQ(d_ff_6_nq));  // open: Q
  LED led_6 (.in(d_ff_6_nq));
  D_FF d_ff_7 (.D(out_1), .C(clk), .nQ(d_ff_7_nq));  // open: Q
  LED led_7 (.in(d_ff_7_nq));
  D_FF d_ff_8 (.D(out_1), .C(clk), .nQ(d_ff_8_nq));  // open: Q
  LED led_8 (.in(d_ff_8_nq));
endmodule
